# Fritzing sketch Rover (saved by Fritzing 0.9.3b)
breadboards: 3

parts:
  Part1 = Arduino Uno (Rev3)
  M6 = DC Motor
  M7 = DC Motor
  M8 = DC Motor
  M9 = DC Motor
  VCC1 = Battery block 9V
  Súčiastka2 = MicroSD Card Module  # not connected
  Súčiastka3 = Adafruit BMP180
  R1 = Resistor [tolerance=±5% resistance=10k package="2512 [SMD]"]
  R2 = Photocell (LDR) [package=THT]
  3-pins_Hall_Effect_Sensor = mystery part, 3 pins [chip_label=TLE]
  R3 = Resistor [tolerance=±5% resistance=10k package="2512 [SMD]"]
  S1 = H-Bridge with L298N
  S2 = H-Bridge with L298N
  DHT1 = DHT22 Humidity and Temperature Sensor
  U1 = NodeMCU V3.0

nets:
  N1: Part1.A3, R1.Pin_0, R2.pin_0
  N2: Part1.A4/SDA, Súčiastka3.SDA
  N3: Part1.A5/SCL, Súčiastka3.SCL
  N4: Part1.D2, 3-pins_Hall_Effect_Sensor.pin3, R3.Pin_1
  N5: Part1.D3_PWM, DHT1.DATA
  5V: Part1.5V, Súčiastka3.+5V, R2.pin_1, 3-pins_Hall_Effect_Sensor.pin1, R3.Pin_0, DHT1.VDD
  GND: Part1.GND, Súčiastka3.GND, R1.Pin_1, 3-pins_Hall_Effect_Sensor.pin2, DHT1.NULL
  N6: M6.pin_1, S2.M1-02
  N7: M6.pin_2, S2.M1-01
  N8: M7.pin_1, S2.M2-02
  N9: M7.pin_2, S2.M2-01
  N10: M8.pin_1, S1.M2-02
  N11: M8.pin_2, S1.M2-01
  N12: M9.pin_1, S1.M1-02
  N13: M9.pin_2, S1.M1-01
  GND_2: VCC1.-, S1.GND, S2.GND, U1.GND
  12V: VCC1.+, S1.12V, S2.12V
  5V_2: S1.5V, S2.5V, U1.3V3
  N14: S1.ENA, S1.ENA-5V
  N15: S1.IN1, S2.IN1, U1.D5
  N16: S1.IN2, S2.IN2, U1.D6
  N17: S1.IN3, S2.IN3, U1.D7
  N18: S1.IN4, S2.IN4, U1.D8
  N19: S1.ENB, S1.ENB-5V
  N20: S2.ENA, S2.ENA-5V
  N21: S2.ENB, S2.ENB-5V

custom parts:
  Adafruit BMP180: This precision sensor from Bosch is the best low-cost sensing solution for measuring barometric pressure and temperature. Because pressure changes with altitude you can also use it as an altimeter! The sensor is soldered onto a PCB with a 3.3V regulator, I2C level shifter and pull-up resistors on the I2C pins. The BMP180 is the next-generation of sensors from Bosch, and replaces the BMP085.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
  H-Bridge with L298N: h-bridge
  NodeMCU V3.0: NodeMcu V3 Lua WIFI Development Board
